# Fritzing sketch Garden_Nomad_Fritzing (saved by Fritzing 1.0.0rc)
breadboards: 1

parts:
  A1 = Particle - Photon2
  S1 = Pushbutton [package="[THT]"]
  S2 = Pushbutton [package="[THT]"]
  S3 = Pushbutton [package="[THT]"]
  S4 = Pushbutton [package="[THT]"]
  S5 = Pushbutton [package="[THT]"]
  S6 = Pushbutton [package="[THT]"]
  R1 = Resistor [tolerance=±5% resistance=10000 package="0805 [SMD]"]
  R2 = Resistor [tolerance=±5% resistance=10000 package="0805 [SMD]"]
  R3 = Resistor [tolerance=±5% resistance=10000 package="0805 [SMD]"]
  R4 = Resistor [tolerance=±5% resistance=10000 package="0805 [SMD]"]
  R5 = Resistor [tolerance=±5% resistance=10000 package="0805 [SMD]"]
  LED1 = smd LED [color="Red (633nm)" package="1206 [SMD]"]
  LED2 = smd LED [color="Red (633nm)" package="1206 [SMD]"]
  R6 = Resistor [tolerance=±5% resistance=220 package="0805 [SMD]"]
  R7 = Resistor [tolerance=±5% resistance=220 package="0805 [SMD]"]
  U1 = LIPO-2000mAh [package=lipo-2000]
  Part1 = VEML7700 [part_number="Adafruit #4162"]
  OLED_I2C1 = OLED 128x64 I2C Monochrome Display
  M1 = BMP280
  M2 = PH meter with sensor in breadboard [package=THT]
  SENS1 = SoilWatch 10

nets:
  VIN: A1.Pin_2, A1.Pin_31, S2.Pin_4, S3.Pin_4, S4.Pin_4, S5.Pin_4, S6.Pin_4, Part1.VIN, OLED_I2C1.VDD, M1.VIN, M2.pin2, SENS1.VCC
  GND: A1.Pin_4, A1.Pin_30, A1.Pin_32, A1.Pin_35, S1.Pin_4, R1.Pin_1, R2.Pin_1, R3.Pin_1, R4.Pin_1, R5.Pin_1, R6.Pin_1, R7.Pin_1, U1.-, Part1.GND, OLED_I2C1.GND, M1.GND, M2.pin3, SENS1.GND
  N1: A1.Pin_6, M2.pin1
  N2: A1.Pin_7, SENS1.OUT
  N3: A1.Pin_17, Part1.SDA, OLED_I2C1.SDA, M1.SDA
  N4: A1.Pin_18, Part1.SCL, OLED_I2C1.SCK, M1.SCL
  N5: A1.Pin_19, LED2.anode
  N6: A1.Pin_20, LED1.anode
  N7: A1.Pin_21, S6.Pin_1, S6.Pin_2, R5.Pin_0
  N8: A1.Pin_22, S5.Pin_1, S5.Pin_2, R4.Pin_0
  N9: A1.Pin_23, S4.Pin_1, S4.Pin_2, R3.Pin_0
  N10: A1.Pin_24, S3.Pin_1, S3.Pin_2, R2.Pin_0
  N11: A1.Pin_25, S2.Pin_1, S2.Pin_2, R1.Pin_0
  N12: A1.Pin_27, S1.Pin_2
  N13: A1.Pin_28, A1.Pin_29, U1.+
  N14: LED1.cathode, R7.Pin_0
  N15: LED2.cathode, R6.Pin_0

custom parts:
  Particle - Photon2: The Photon 2 is a microcontroller and Wi-Fi networking developed by particle. Features: 802.11a/b/g/n Wi-Fi, 2.4 GHz and 5 GHz Integrated PCB antenna Integrated U.FL connector for external antenna Integrated RF switch BLE 5 using same antenna as Wi-Fi Realtek RTL8721DM MCU ARM Cortex M33 CPU, 200 MHz 2048 KB (2 MB) user application maximum size 3072 KB (3 MB) of RAM available to user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
  Pushbutton: A generic pushbutton.
  BMP280: Temperature Humidity Barometric presure Sensor, I2C
  PH meter with sensor in breadboard: DFrobot PH meter (SKU SEN0161)
  SoilWatch 10: SoilWatch 10 - Capacitive soil moisture sensor
